// Logisim project Mano basic Computer .circ as structural Verilog: 8 circuits, main circuit main
// AR
module main (
  input  S2,
  input  S1,
  input  S0
);

  wire clock_1_out, control_unit_1_clr_ar, control_unit_1_inc_ar, control_unit_1_ld_ar, decoder_1_out0,
       decoder_1_out1, decoder_1_out2, decoder_1_out3, decoder_1_out4, decoder_1_out5, decoder_1_out6,
       decoder_1_out7, decoder_2_out0, decoder_2_out1, decoder_2_out2, decoder_2_out3, decoder_2_out4,
       decoder_2_out5, decoder_2_out6, decoder_2_out7, decoder_2_out8, decoder_2_out9, decoder_2_out10,
       decoder_2_out11, decoder_2_out12, decoder_2_out13, decoder_2_out14, decoder_2_out15, FGI_q, FGO_q,
       I_q, IEN_q;
  wire [3:0] counter_1_q;
  wire [11:0] Address;
  wire [15:0] AC, AR, DR, IR, M_AR, multiplexer_1_out, PC, TR, undriven;

  Counter #(.width(4), .max('hf)) counter_1 (.Q(counter_1_q), .clk(clock_1_out));  // open: load, D, count, carry, clr
  Clock clock_1 (.out(clock_1_out));
  D_Flip_Flop I (.clk(clock_1_out), .D(undriven[15]), .Q(I_q));  // open: Qn, preset, en, reset
  Decoder #(.select(3)) decoder_1 (
    .out0(decoder_1_out0), .out1(decoder_1_out1), .out2(decoder_1_out2), .out3(decoder_1_out3),
    .out4(decoder_1_out4), .out5(decoder_1_out5), .out6(decoder_1_out6), .out7(decoder_1_out7),
    .sel(undriven[14:12]));  // open: en
  Decoder #(.select(4)) decoder_2 (
    .out0(decoder_2_out0), .out1(decoder_2_out1), .out2(decoder_2_out2), .out3(decoder_2_out3),
    .out4(decoder_2_out4), .out5(decoder_2_out5), .out6(decoder_2_out6), .out7(decoder_2_out7),
    .out8(decoder_2_out8), .out9(decoder_2_out9), .out10(decoder_2_out10), .out11(decoder_2_out11),
    .out12(decoder_2_out12), .out13(decoder_2_out13), .out14(decoder_2_out14), .out15(decoder_2_out15),
    .sel(counter_1_q));  // open: en
  FlipFlop FGI (.Q(FGI_q));  // open: Clk, D, set, Clr
  FlipFlop IEN (.Q(IEN_q));  // open: Clk, D, set, Clr
  FlipFlop FGO (.Q(FGO_q));  // open: Clk, D, set, Clr
  Control_Unit control_unit_1 (
    ._0_11(undriven[11:0]), .D0(decoder_1_out0), .D1(decoder_1_out1), .D2(decoder_1_out2),
    .D3(decoder_1_out3), .D4(decoder_1_out4), .D5(decoder_1_out5), .D6(decoder_1_out6), .D7(decoder_1_out7),
    .I(I_q), .T0(decoder_2_out15), .T1(decoder_2_out14), .T2(decoder_2_out13), .T3(decoder_2_out12),
    .T4(decoder_2_out11), .T5(decoder_2_out10), .T6(decoder_2_out9), .T7(decoder_2_out8),
    .T8(decoder_2_out7), .T9(decoder_2_out6), .T10(decoder_2_out5), .T11(decoder_2_out4),
    .T12(decoder_2_out3), .T13(decoder_2_out2), .T14(decoder_2_out1), .T15(decoder_2_out0), .FGI(FGI_q),
    .FGO(FGO_q), .IEN(IEN_q), .LD_AR(control_unit_1_ld_ar), .CLR_AR(control_unit_1_clr_ar),
    .INC_AR(control_unit_1_inc_ar));  // open: R
  AR u_AR (
    .Clk(clock_1_out), .INC(control_unit_1_inc_ar), .LD(control_unit_1_ld_ar), .CLR(control_unit_1_clr_ar),
    .Address(Address), .Bus_Out(AR));  // open: Bus_In
  Rigester_12bit u_PC (.Bus_Out(PC));  // open: Clk, INC, LD, CLR, Bus_In
  Register_16bit u_DR (.Q(DR));  // open: Clk, INC, LD, CLR, Data, cout
  Register_16bit u_AC (.Q(AC));  // open: Clk, INC, LD, CLR, Data, cout
  Register_16bit u_IR (.Q(IR));  // open: Clk, INC, LD, CLR, Data, cout
  Register_16bit u_TR (.Q(TR));  // open: Clk, INC, LD, CLR, Data, cout
  RAM #(.addrWidth(12), .dataWidth(16), .bus("separate")) ram_1 (
    .addr(Address), .din(multiplexer_1_out), .data(M_AR), .clk(clock_1_out));  // open: str, sel, ld, clr
  Multiplexer #(.select(3), .width(16)) multiplexer_1 (
    .in1(AR), .in2(PC), .in3(DR), .in4(AC), .in5(IR), .in6(TR), .in7(M_AR), .out(multiplexer_1_out),
    .sel({S2, S1, S0}));  // open: in0, en
endmodule

module Register_16bit (
  input  Clk,
  input  INC,
  input  LD,
  input  CLR,
  input  [15:0] Data,
  output cout,
  output [15:0] Q
);

  wire adder_1_out, adder_2_cout, adder_2_out, adder_3_cout, adder_3_out, adder_4_cout, adder_4_out,
       adder_5_cout, adder_5_out, adder_6_cout, adder_6_out, adder_7_cout, adder_7_out, adder_8_cout,
       adder_8_out, adder_9_cout, adder_9_out, adder_10_cout, adder_10_out, adder_11_cout, adder_11_out,
       adder_12_cout, adder_12_out, adder_13_cout, adder_13_out, adder_14_cout, adder_14_out, adder_15_cout,
       adder_15_out, adder_16_cout, adder_16_out, multiplexer_1_out, multiplexer_2_out, multiplexer_3_out,
       multiplexer_4_out, multiplexer_5_out, multiplexer_6_out, multiplexer_7_out, multiplexer_8_out,
       multiplexer_9_out, multiplexer_10_out, multiplexer_11_out, multiplexer_12_out, multiplexer_13_out,
       multiplexer_14_out, multiplexer_15_out, multiplexer_16_out;
  wire [1:0] priority_encoder_1_out;

  Priority_Encoder #(.select(2)) priority_encoder_1 (
    .in1(INC), .in2(LD), .in3(CLR), .out(priority_encoder_1_out));  // open: in0, gs, en_out, en_in
  Adder #(.width(1)) adder_1 (.a(Q[15]), .b(adder_2_cout), .out(adder_1_out), .cout(cout));  // open: cin
  Adder #(.width(1)) adder_2 (.a(Q[14]), .b(adder_3_cout), .out(adder_2_out), .cout(adder_2_cout));  // open: cin
  Adder #(.width(1)) adder_3 (.a(Q[13]), .b(adder_4_cout), .out(adder_3_out), .cout(adder_3_cout));  // open: cin
  Adder #(.width(1)) adder_4 (.a(Q[12]), .b(adder_5_cout), .out(adder_4_out), .cout(adder_4_cout));  // open: cin
  Adder #(.width(1)) adder_5 (.a(Q[11]), .b(adder_6_cout), .out(adder_5_out), .cout(adder_5_cout));  // open: cin
  Adder #(.width(1)) adder_6 (.a(Q[10]), .b(adder_7_cout), .out(adder_6_out), .cout(adder_6_cout));  // open: cin
  Adder #(.width(1)) adder_7 (.a(Q[9]), .b(adder_8_cout), .out(adder_7_out), .cout(adder_7_cout));  // open: cin
  Adder #(.width(1)) adder_8 (.a(Q[8]), .b(adder_9_cout), .out(adder_8_out), .cout(adder_8_cout));  // open: cin
  Adder #(.width(1)) adder_9 (.a(Q[7]), .b(adder_10_cout), .out(adder_9_out), .cout(adder_9_cout));  // open: cin
  Adder #(.width(1)) adder_10 (.a(Q[6]), .b(adder_11_cout), .out(adder_10_out), .cout(adder_10_cout));  // open: cin
  Adder #(.width(1)) adder_11 (.a(Q[5]), .b(adder_12_cout), .out(adder_11_out), .cout(adder_11_cout));  // open: cin
  Adder #(.width(1)) adder_12 (.a(Q[4]), .b(adder_13_cout), .out(adder_12_out), .cout(adder_12_cout));  // open: cin
  Adder #(.width(1)) adder_13 (.a(Q[3]), .b(adder_14_cout), .out(adder_13_out), .cout(adder_13_cout));  // open: cin
  Adder #(.width(1)) adder_14 (.a(Q[2]), .b(adder_15_cout), .out(adder_14_out), .cout(adder_14_cout));  // open: cin
  Adder #(.width(1)) adder_15 (.a(Q[1]), .b(adder_16_cout), .out(adder_15_out), .cout(adder_15_cout));  // open: cin
  Adder #(.width(1)) adder_16 (.a(Q[0]), .b(1'b1), .out(adder_16_out), .cout(adder_16_cout));  // open: cin
  Multiplexer #(.select(2)) multiplexer_1 (
    .in1(adder_1_out), .in2(Data[15]), .in3(1'b0), .out(multiplexer_1_out), .sel(priority_encoder_1_out));  // open: in0, en
  Multiplexer #(.select(2)) multiplexer_2 (
    .in1(adder_2_out), .in2(Data[14]), .in3(1'b0), .out(multiplexer_2_out), .sel(priority_encoder_1_out));  // open: in0, en
  Multiplexer #(.select(2)) multiplexer_3 (
    .in1(adder_3_out), .in2(Data[13]), .in3(1'b0), .out(multiplexer_3_out), .sel(priority_encoder_1_out));  // open: in0, en
  Multiplexer #(.select(2)) multiplexer_4 (
    .in1(adder_4_out), .in2(Data[12]), .in3(1'b0), .out(multiplexer_4_out), .sel(priority_encoder_1_out));  // open: in0, en
  Multiplexer #(.select(2)) multiplexer_5 (
    .in1(adder_5_out), .in2(Data[11]), .in3(1'b0), .out(multiplexer_5_out), .sel(priority_encoder_1_out));  // open: in0, en
  Multiplexer #(.select(2)) multiplexer_6 (
    .in1(adder_6_out), .in2(Data[10]), .in3(1'b0), .out(multiplexer_6_out), .sel(priority_encoder_1_out));  // open: in0, en
  Multiplexer #(.select(2)) multiplexer_7 (
    .in1(adder_7_out), .in2(Data[9]), .in3(1'b0), .out(multiplexer_7_out), .sel(priority_encoder_1_out));  // open: in0, en
  Multiplexer #(.select(2)) multiplexer_8 (
    .in1(adder_8_out), .in2(Data[8]), .in3(1'b0), .out(multiplexer_8_out), .sel(priority_encoder_1_out));  // open: in0, en
  Multiplexer #(.select(2)) multiplexer_9 (
    .in1(adder_9_out), .in2(Data[7]), .in3(1'b0), .out(multiplexer_9_out), .sel(priority_encoder_1_out));  // open: in0, en
  Multiplexer #(.select(2)) multiplexer_10 (
    .in1(adder_10_out), .in2(Data[6]), .in3(1'b0), .out(multiplexer_10_out), .sel(priority_encoder_1_out));  // open: in0, en
  Multiplexer #(.select(2)) multiplexer_11 (
    .in1(adder_11_out), .in2(Data[5]), .in3(1'b0), .out(multiplexer_11_out), .sel(priority_encoder_1_out));  // open: in0, en
  Multiplexer #(.select(2)) multiplexer_12 (
    .in1(adder_12_out), .in2(Data[4]), .in3(1'b0), .out(multiplexer_12_out), .sel(priority_encoder_1_out));  // open: in0, en
  Multiplexer #(.select(2)) multiplexer_13 (
    .in1(adder_13_out), .in2(Data[3]), .in3(1'b0), .out(multiplexer_13_out), .sel(priority_encoder_1_out));  // open: in0, en
  Multiplexer #(.select(2)) multiplexer_14 (
    .in1(adder_14_out), .in2(Data[2]), .in3(1'b0), .out(multiplexer_14_out), .sel(priority_encoder_1_out));  // open: in0, en
  Multiplexer #(.select(2)) multiplexer_15 (
    .in1(adder_15_out), .in2(Data[1]), .in3(1'b0), .out(multiplexer_15_out), .sel(priority_encoder_1_out));  // open: in0, en
  Multiplexer #(.select(2)) multiplexer_16 (
    .in1(adder_16_out), .in2(Data[0]), .in3(1'b0), .out(multiplexer_16_out), .sel(priority_encoder_1_out));  // open: in0, en
  D_Flip_Flop d_ff_1 (.clk(Clk), .D(multiplexer_1_out), .Q(Q[15]));  // open: Qn, preset, en, reset
  D_Flip_Flop d_ff_2 (.clk(Clk), .D(multiplexer_2_out), .Q(Q[14]));  // open: Qn, preset, en, reset
  D_Flip_Flop d_ff_3 (.clk(Clk), .D(multiplexer_3_out), .Q(Q[13]));  // open: Qn, preset, en, reset
  D_Flip_Flop d_ff_4 (.clk(Clk), .D(multiplexer_4_out), .Q(Q[12]));  // open: Qn, preset, en, reset
  D_Flip_Flop d_ff_5 (.clk(Clk), .D(multiplexer_5_out), .Q(Q[11]));  // open: Qn, preset, en, reset
  D_Flip_Flop d_ff_6 (.clk(Clk), .D(multiplexer_6_out), .Q(Q[10]));  // open: Qn, preset, en, reset
  D_Flip_Flop d_ff_7 (.clk(Clk), .D(multiplexer_7_out), .Q(Q[9]));  // open: Qn, preset, en, reset
  D_Flip_Flop d_ff_8 (.clk(Clk), .D(multiplexer_8_out), .Q(Q[8]));  // open: Qn, preset, en, reset
  D_Flip_Flop d_ff_9 (.clk(Clk), .D(multiplexer_9_out), .Q(Q[7]));  // open: Qn, preset, en, reset
  D_Flip_Flop d_ff_10 (.clk(Clk), .D(multiplexer_10_out), .Q(Q[6]));  // open: Qn, preset, en, reset
  D_Flip_Flop d_ff_11 (.clk(Clk), .D(multiplexer_11_out), .Q(Q[5]));  // open: Qn, preset, en, reset
  D_Flip_Flop d_ff_12 (.clk(Clk), .D(multiplexer_12_out), .Q(Q[4]));  // open: Qn, preset, en, reset
  D_Flip_Flop d_ff_13 (.clk(Clk), .D(multiplexer_13_out), .Q(Q[3]));  // open: Qn, preset, en, reset
  D_Flip_Flop d_ff_14 (.clk(Clk), .D(multiplexer_14_out), .Q(Q[2]));  // open: Qn, preset, en, reset
  D_Flip_Flop d_ff_15 (.clk(Clk), .D(multiplexer_15_out), .Q(Q[1]));  // open: Qn, preset, en, reset
  D_Flip_Flop d_ff_16 (.clk(Clk), .D(multiplexer_16_out), .Q(Q[0]));  // open: Qn, preset, en, reset
endmodule

module Control_Unit (
  input  [11:0] _0_11,
  input  D0,
  input  D1,
  input  D2,
  input  D3,
  input  D4,
  input  D5,
  input  D6,
  input  D7,
  input  I,
  input  T0,
  input  T1,
  input  T2,
  input  T3,
  input  T4,
  input  T5,
  input  T6,
  input  T7,
  input  T8,
  input  T9,
  input  T10,
  input  T11,
  input  T12,
  input  T13,
  input  T14,
  input  T15,
  input  FGI,
  input  FGO,
  input  IEN,
  output LD_AR,
  output CLR_AR,
  output INC_AR,
  output R
);

  wire and_1_out, and_2_out, or_1_out;

  or or_1 (or_1_out, FGI, FGO);
  and and_1 (and_1_out, or_1_out, IEN);
  and and_2 (and_2_out, ~T0, ~T1, ~T2);  // AND_Gate
  and and_3 (R, and_1_out, and_2_out);
  Control_AR control_ar_1 (
    .R(R), .T0(T0), .T2(T2), .T3(T3), .I(I), .D7(D7), .D5(D5), .T4(T4), .LD(LD_AR), .CLR(CLR_AR), .INR(INC_AR));

  // Other names for the same wires on the sheet: B0 = _0_11[0]; B1 = _0_11[1]; B2 = _0_11[2]; B3 = _0_11[3];
  //   B4 = _0_11[4]; B5 = _0_11[5]; B6 = _0_11[6]; B7 = _0_11[7]; B8 = _0_11[8]; B9 = _0_11[9]; B10 = _0_11[10];
  //   B11 = _0_11[11]
endmodule

module Rigester_12bit (
  input  Clk,
  input  INC,
  input  LD,
  input  CLR,
  input  [15:0] Bus_In,
  output [15:0] Bus_Out
);

  wire adder_1_out, adder_2_cout, adder_2_out, adder_3_cout, adder_3_out, adder_4_cout, adder_4_out,
       adder_5_cout, adder_5_out, adder_6_cout, adder_6_out, adder_7_cout, adder_7_out, adder_8_cout,
       adder_8_out, adder_9_cout, adder_9_out, adder_10_cout, adder_10_out, adder_11_cout, adder_11_out,
       adder_12_cout, adder_12_out, multiplexer_1_out, multiplexer_2_out, multiplexer_3_out,
       multiplexer_4_out, multiplexer_5_out, multiplexer_6_out, multiplexer_7_out, multiplexer_8_out,
       multiplexer_9_out, multiplexer_10_out, multiplexer_11_out, multiplexer_12_out;
  wire [1:0] priority_encoder_1_out;

  Priority_Encoder #(.select(2)) priority_encoder_1 (
    .in0(1'b0), .in1(INC), .in2(LD), .in3(CLR), .out(priority_encoder_1_out));  // open: gs, en_out, en_in
  Adder #(.width(1)) adder_1 (.a(Bus_Out[11]), .b(adder_2_cout), .out(adder_1_out));  // open: cin, cout
  Adder #(.width(1)) adder_2 (.a(Bus_Out[10]), .b(adder_3_cout), .out(adder_2_out), .cout(adder_2_cout));  // open: cin
  Adder #(.width(1)) adder_3 (.a(Bus_Out[9]), .b(adder_4_cout), .out(adder_3_out), .cout(adder_3_cout));  // open: cin
  Adder #(.width(1)) adder_4 (.a(Bus_Out[8]), .b(adder_5_cout), .out(adder_4_out), .cout(adder_4_cout));  // open: cin
  Adder #(.width(1)) adder_5 (.a(Bus_Out[7]), .b(adder_6_cout), .out(adder_5_out), .cout(adder_5_cout));  // open: cin
  Adder #(.width(1)) adder_6 (.a(Bus_Out[6]), .b(adder_7_cout), .out(adder_6_out), .cout(adder_6_cout));  // open: cin
  Adder #(.width(1)) adder_7 (.a(Bus_Out[5]), .b(adder_8_cout), .out(adder_7_out), .cout(adder_7_cout));  // open: cin
  Adder #(.width(1)) adder_8 (.a(Bus_Out[4]), .b(adder_9_cout), .out(adder_8_out), .cout(adder_8_cout));  // open: cin
  Adder #(.width(1)) adder_9 (.a(Bus_Out[3]), .b(adder_10_cout), .out(adder_9_out), .cout(adder_9_cout));  // open: cin
  Adder #(.width(1)) adder_10 (
    .a(Bus_Out[2]), .b(adder_11_cout), .out(adder_10_out), .cout(adder_10_cout));  // open: cin
  Adder #(.width(1)) adder_11 (
    .a(Bus_Out[1]), .b(adder_12_cout), .out(adder_11_out), .cout(adder_11_cout));  // open: cin
  Adder #(.width(1)) adder_12 (.a(Bus_Out[0]), .b(1'b1), .out(adder_12_out), .cout(adder_12_cout));  // open: cin
  Multiplexer #(.select(2)) multiplexer_1 (
    .in1(adder_1_out), .in2(Bus_In[11]), .in3(1'b0), .out(multiplexer_1_out), .sel(priority_encoder_1_out));  // open: in0, en
  Multiplexer #(.select(2)) multiplexer_2 (
    .in1(adder_2_out), .in2(Bus_In[10]), .in3(1'b0), .out(multiplexer_2_out), .sel(priority_encoder_1_out));  // open: in0, en
  Multiplexer #(.select(2)) multiplexer_3 (
    .in1(adder_3_out), .in2(Bus_In[9]), .in3(1'b0), .out(multiplexer_3_out), .sel(priority_encoder_1_out));  // open: in0, en
  Multiplexer #(.select(2)) multiplexer_4 (
    .in1(adder_4_out), .in2(Bus_In[8]), .in3(1'b0), .out(multiplexer_4_out), .sel(priority_encoder_1_out));  // open: in0, en
  Multiplexer #(.select(2)) multiplexer_5 (
    .in1(adder_5_out), .in2(Bus_In[7]), .in3(1'b0), .out(multiplexer_5_out), .sel(priority_encoder_1_out));  // open: in0, en
  Multiplexer #(.select(2)) multiplexer_6 (
    .in1(adder_6_out), .in2(Bus_In[6]), .in3(1'b0), .out(multiplexer_6_out), .sel(priority_encoder_1_out));  // open: in0, en
  Multiplexer #(.select(2)) multiplexer_7 (
    .in1(adder_7_out), .in2(Bus_In[5]), .in3(1'b0), .out(multiplexer_7_out), .sel(priority_encoder_1_out));  // open: in0, en
  Multiplexer #(.select(2)) multiplexer_8 (
    .in1(adder_8_out), .in2(Bus_In[4]), .in3(1'b0), .out(multiplexer_8_out), .sel(priority_encoder_1_out));  // open: in0, en
  Multiplexer #(.select(2)) multiplexer_9 (
    .in1(adder_9_out), .in2(Bus_In[3]), .in3(1'b0), .out(multiplexer_9_out), .sel(priority_encoder_1_out));  // open: in0, en
  Multiplexer #(.select(2)) multiplexer_10 (
    .in1(adder_10_out), .in2(Bus_In[2]), .in3(1'b0), .out(multiplexer_10_out), .sel(priority_encoder_1_out));  // open: in0, en
  Multiplexer #(.select(2)) multiplexer_11 (
    .in1(adder_11_out), .in2(Bus_In[1]), .in3(1'b0), .out(multiplexer_11_out), .sel(priority_encoder_1_out));  // open: in0, en
  Multiplexer #(.select(2)) multiplexer_12 (
    .in1(adder_12_out), .in2(Bus_In[0]), .in3(1'b0), .out(multiplexer_12_out), .sel(priority_encoder_1_out));  // open: in0, en
  D_Flip_Flop d_ff_1 (.clk(Clk), .D(multiplexer_1_out), .Q(Bus_Out[11]));  // open: Qn, preset, en, reset
  D_Flip_Flop d_ff_2 (.clk(Clk), .D(multiplexer_2_out), .Q(Bus_Out[10]));  // open: Qn, preset, en, reset
  D_Flip_Flop d_ff_3 (.clk(Clk), .D(multiplexer_3_out), .Q(Bus_Out[9]));  // open: Qn, preset, en, reset
  D_Flip_Flop d_ff_4 (.clk(Clk), .D(multiplexer_4_out), .Q(Bus_Out[8]));  // open: Qn, preset, en, reset
  D_Flip_Flop d_ff_5 (.clk(Clk), .D(multiplexer_5_out), .Q(Bus_Out[7]));  // open: Qn, preset, en, reset
  D_Flip_Flop d_ff_6 (.clk(Clk), .D(multiplexer_6_out), .Q(Bus_Out[6]));  // open: Qn, preset, en, reset
  D_Flip_Flop d_ff_7 (.clk(Clk), .D(multiplexer_7_out), .Q(Bus_Out[5]));  // open: Qn, preset, en, reset
  D_Flip_Flop d_ff_8 (.clk(Clk), .D(multiplexer_8_out), .Q(Bus_Out[4]));  // open: Qn, preset, en, reset
  D_Flip_Flop d_ff_9 (.clk(Clk), .D(multiplexer_9_out), .Q(Bus_Out[3]));  // open: Qn, preset, en, reset
  D_Flip_Flop d_ff_10 (.clk(Clk), .D(multiplexer_10_out), .Q(Bus_Out[2]));  // open: Qn, preset, en, reset
  D_Flip_Flop d_ff_11 (.clk(Clk), .D(multiplexer_11_out), .Q(Bus_Out[1]));  // open: Qn, preset, en, reset
  D_Flip_Flop d_ff_12 (.clk(Clk), .D(multiplexer_12_out), .Q(Bus_Out[0]));  // open: Qn, preset, en, reset

  assign Bus_In[14:12] = {3{Bus_In[15]}};
  assign Bus_Out[15:12] = 4'b0000;
  // also tied to GND on the sheet: Bus_In[15]
endmodule

module Register_8bit (
  input  Clk,
  input  INC,
  input  LD,
  input  CLR,
  input  [15:0] Bus_In,
  output [15:0] Bus_Out
);

  wire adder_1_cout, adder_1_out, adder_2_cout, adder_2_out, adder_3_cout, adder_3_out, adder_4_cout,
       adder_4_out, adder_5_cout, adder_5_out, adder_6_cout, adder_6_out, adder_7_cout, adder_7_out,
       adder_8_cout, adder_8_out, multiplexer_1_out, multiplexer_2_out, multiplexer_3_out, multiplexer_4_out,
       multiplexer_5_out, multiplexer_6_out, multiplexer_7_out, multiplexer_8_out;
  wire [1:0] priority_encoder_1_out;

  Priority_Encoder #(.select(2)) priority_encoder_1 (
    .in0(1'b0), .in1(INC), .in2(LD), .in3(CLR), .out(priority_encoder_1_out));  // open: gs, en_out, en_in
  Adder #(.width(1)) adder_1 (.a(Bus_Out[7]), .b(adder_2_cout), .out(adder_1_out), .cout(adder_1_cout));  // open: cin
  Adder #(.width(1)) adder_2 (.a(Bus_Out[6]), .b(adder_3_cout), .out(adder_2_out), .cout(adder_2_cout));  // open: cin
  Adder #(.width(1)) adder_3 (.a(Bus_Out[5]), .b(adder_4_cout), .out(adder_3_out), .cout(adder_3_cout));  // open: cin
  Adder #(.width(1)) adder_4 (.a(Bus_Out[4]), .b(adder_5_cout), .out(adder_4_out), .cout(adder_4_cout));  // open: cin
  Adder #(.width(1)) adder_5 (.a(Bus_Out[3]), .b(adder_6_cout), .out(adder_5_out), .cout(adder_5_cout));  // open: cin
  Adder #(.width(1)) adder_6 (.a(Bus_Out[2]), .b(adder_7_cout), .out(adder_6_out), .cout(adder_6_cout));  // open: cin
  Adder #(.width(1)) adder_7 (.a(Bus_Out[1]), .b(adder_8_cout), .out(adder_7_out), .cout(adder_7_cout));  // open: cin
  Adder #(.width(1)) adder_8 (.a(Bus_Out[0]), .b(1'b1), .out(adder_8_out), .cout(adder_8_cout));  // open: cin
  Multiplexer #(.select(2)) multiplexer_1 (
    .in1(adder_1_out), .in2(Bus_In[7]), .in3(1'b0), .out(multiplexer_1_out), .sel(priority_encoder_1_out));  // open: in0, en
  Multiplexer #(.select(2)) multiplexer_2 (
    .in1(adder_2_out), .in2(Bus_In[6]), .in3(1'b0), .out(multiplexer_2_out), .sel(priority_encoder_1_out));  // open: in0, en
  Multiplexer #(.select(2)) multiplexer_3 (
    .in1(adder_3_out), .in2(Bus_In[5]), .in3(1'b0), .out(multiplexer_3_out), .sel(priority_encoder_1_out));  // open: in0, en
  Multiplexer #(.select(2)) multiplexer_4 (
    .in1(adder_4_out), .in2(Bus_In[4]), .in3(1'b0), .out(multiplexer_4_out), .sel(priority_encoder_1_out));  // open: in0, en
  Multiplexer #(.select(2)) multiplexer_5 (
    .in1(adder_5_out), .in2(Bus_In[3]), .in3(1'b0), .out(multiplexer_5_out), .sel(priority_encoder_1_out));  // open: in0, en
  Multiplexer #(.select(2)) multiplexer_6 (
    .in1(adder_6_out), .in2(Bus_In[2]), .in3(1'b0), .out(multiplexer_6_out), .sel(priority_encoder_1_out));  // open: in0, en
  Multiplexer #(.select(2)) multiplexer_7 (
    .in1(adder_7_out), .in2(Bus_In[1]), .in3(1'b0), .out(multiplexer_7_out), .sel(priority_encoder_1_out));  // open: in0, en
  Multiplexer #(.select(2)) multiplexer_8 (
    .in1(adder_8_out), .in2(Bus_In[0]), .in3(1'b0), .out(multiplexer_8_out), .sel(priority_encoder_1_out));  // open: in0, en
  D_Flip_Flop d_ff_1 (.clk(Clk), .D(multiplexer_1_out), .Q(Bus_Out[7]));  // open: Qn, preset, en, reset
  D_Flip_Flop d_ff_2 (.clk(Clk), .D(multiplexer_2_out), .Q(Bus_Out[6]));  // open: Qn, preset, en, reset
  D_Flip_Flop d_ff_3 (.clk(Clk), .D(multiplexer_3_out), .Q(Bus_Out[5]));  // open: Qn, preset, en, reset
  D_Flip_Flop d_ff_4 (.clk(Clk), .D(multiplexer_4_out), .Q(Bus_Out[4]));  // open: Qn, preset, en, reset
  D_Flip_Flop d_ff_5 (.clk(Clk), .D(multiplexer_5_out), .Q(Bus_Out[3]));  // open: Qn, preset, en, reset
  D_Flip_Flop d_ff_6 (.clk(Clk), .D(multiplexer_6_out), .Q(Bus_Out[2]));  // open: Qn, preset, en, reset
  D_Flip_Flop d_ff_7 (.clk(Clk), .D(multiplexer_7_out), .Q(Bus_Out[1]));  // open: Qn, preset, en, reset
  D_Flip_Flop d_ff_8 (.clk(Clk), .D(multiplexer_8_out), .Q(Bus_Out[0]));  // open: Qn, preset, en, reset

  assign Bus_In[14:8] = {7{Bus_In[15]}};
  assign Bus_Out[15:8] = {8{1'b0}};
  // also tied to GND on the sheet: Bus_In[15]
endmodule

module AR (
  input  Clk,
  input  INC,
  input  LD,
  input  CLR,
  input  [15:0] Bus_In,
  output [11:0] Address,
  output [15:0] Bus_Out
);

  wire adder_1_out, adder_2_cout, adder_2_out, adder_3_cout, adder_3_out, adder_4_cout, adder_4_out,
       adder_5_cout, adder_5_out, adder_6_cout, adder_6_out, adder_7_cout, adder_7_out, adder_8_cout,
       adder_8_out, adder_9_cout, adder_9_out, adder_10_cout, adder_10_out, adder_11_cout, adder_11_out,
       adder_12_cout, adder_12_out, multiplexer_1_out, multiplexer_2_out, multiplexer_3_out,
       multiplexer_4_out, multiplexer_5_out, multiplexer_6_out, multiplexer_7_out, multiplexer_8_out,
       multiplexer_9_out, multiplexer_10_out, multiplexer_11_out, multiplexer_12_out;
  wire [1:0] priority_encoder_1_out;

  Priority_Encoder #(.select(2)) priority_encoder_1 (
    .in0(1'b0), .in1(INC), .in2(LD), .in3(CLR), .out(priority_encoder_1_out));  // open: gs, en_out, en_in
  Adder #(.width(1)) adder_1 (.a(Address[11]), .b(adder_2_cout), .out(adder_1_out));  // open: cin, cout
  Adder #(.width(1)) adder_2 (.a(Address[10]), .b(adder_3_cout), .out(adder_2_out), .cout(adder_2_cout));  // open: cin
  Adder #(.width(1)) adder_3 (.a(Address[9]), .b(adder_4_cout), .out(adder_3_out), .cout(adder_3_cout));  // open: cin
  Adder #(.width(1)) adder_4 (.a(Address[8]), .b(adder_5_cout), .out(adder_4_out), .cout(adder_4_cout));  // open: cin
  Adder #(.width(1)) adder_5 (.a(Address[7]), .b(adder_6_cout), .out(adder_5_out), .cout(adder_5_cout));  // open: cin
  Adder #(.width(1)) adder_6 (.a(Address[6]), .b(adder_7_cout), .out(adder_6_out), .cout(adder_6_cout));  // open: cin
  Adder #(.width(1)) adder_7 (.a(Address[5]), .b(adder_8_cout), .out(adder_7_out), .cout(adder_7_cout));  // open: cin
  Adder #(.width(1)) adder_8 (.a(Address[4]), .b(adder_9_cout), .out(adder_8_out), .cout(adder_8_cout));  // open: cin
  Adder #(.width(1)) adder_9 (.a(Address[3]), .b(adder_10_cout), .out(adder_9_out), .cout(adder_9_cout));  // open: cin
  Adder #(.width(1)) adder_10 (
    .a(Address[2]), .b(adder_11_cout), .out(adder_10_out), .cout(adder_10_cout));  // open: cin
  Adder #(.width(1)) adder_11 (
    .a(Address[1]), .b(adder_12_cout), .out(adder_11_out), .cout(adder_11_cout));  // open: cin
  Adder #(.width(1)) adder_12 (.a(Address[0]), .b(1'b1), .out(adder_12_out), .cout(adder_12_cout));  // open: cin
  Multiplexer #(.select(2)) multiplexer_1 (
    .in1(adder_1_out), .in2(Bus_In[11]), .in3(1'b0), .out(multiplexer_1_out), .sel(priority_encoder_1_out));  // open: in0, en
  Multiplexer #(.select(2)) multiplexer_2 (
    .in1(adder_2_out), .in2(Bus_In[10]), .in3(1'b0), .out(multiplexer_2_out), .sel(priority_encoder_1_out));  // open: in0, en
  Multiplexer #(.select(2)) multiplexer_3 (
    .in1(adder_3_out), .in2(Bus_In[9]), .in3(1'b0), .out(multiplexer_3_out), .sel(priority_encoder_1_out));  // open: in0, en
  Multiplexer #(.select(2)) multiplexer_4 (
    .in1(adder_4_out), .in2(Bus_In[8]), .in3(1'b0), .out(multiplexer_4_out), .sel(priority_encoder_1_out));  // open: in0, en
  Multiplexer #(.select(2)) multiplexer_5 (
    .in1(adder_5_out), .in2(Bus_In[7]), .in3(1'b0), .out(multiplexer_5_out), .sel(priority_encoder_1_out));  // open: in0, en
  Multiplexer #(.select(2)) multiplexer_6 (
    .in1(adder_6_out), .in2(Bus_In[6]), .in3(1'b0), .out(multiplexer_6_out), .sel(priority_encoder_1_out));  // open: in0, en
  Multiplexer #(.select(2)) multiplexer_7 (
    .in1(adder_7_out), .in2(Bus_In[5]), .in3(1'b0), .out(multiplexer_7_out), .sel(priority_encoder_1_out));  // open: in0, en
  Multiplexer #(.select(2)) multiplexer_8 (
    .in1(adder_8_out), .in2(Bus_In[4]), .in3(1'b0), .out(multiplexer_8_out), .sel(priority_encoder_1_out));  // open: in0, en
  Multiplexer #(.select(2)) multiplexer_9 (
    .in1(adder_9_out), .in2(Bus_In[3]), .in3(1'b0), .out(multiplexer_9_out), .sel(priority_encoder_1_out));  // open: in0, en
  Multiplexer #(.select(2)) multiplexer_10 (
    .in1(adder_10_out), .in2(Bus_In[2]), .in3(1'b0), .out(multiplexer_10_out), .sel(priority_encoder_1_out));  // open: in0, en
  Multiplexer #(.select(2)) multiplexer_11 (
    .in1(adder_11_out), .in2(Bus_In[1]), .in3(1'b0), .out(multiplexer_11_out), .sel(priority_encoder_1_out));  // open: in0, en
  Multiplexer #(.select(2)) multiplexer_12 (
    .in1(adder_12_out), .in2(Bus_In[0]), .in3(1'b0), .out(multiplexer_12_out), .sel(priority_encoder_1_out));  // open: in0, en
  D_Flip_Flop d_ff_1 (.clk(Clk), .D(multiplexer_1_out), .Q(Address[11]));  // open: Qn, preset, en, reset
  D_Flip_Flop d_ff_2 (.clk(Clk), .D(multiplexer_2_out), .Q(Address[10]));  // open: Qn, preset, en, reset
  D_Flip_Flop d_ff_3 (.clk(Clk), .D(multiplexer_3_out), .Q(Address[9]));  // open: Qn, preset, en, reset
  D_Flip_Flop d_ff_4 (.clk(Clk), .D(multiplexer_4_out), .Q(Address[8]));  // open: Qn, preset, en, reset
  D_Flip_Flop d_ff_5 (.clk(Clk), .D(multiplexer_5_out), .Q(Address[7]));  // open: Qn, preset, en, reset
  D_Flip_Flop d_ff_6 (.clk(Clk), .D(multiplexer_6_out), .Q(Address[6]));  // open: Qn, preset, en, reset
  D_Flip_Flop d_ff_7 (.clk(Clk), .D(multiplexer_7_out), .Q(Address[5]));  // open: Qn, preset, en, reset
  D_Flip_Flop d_ff_8 (.clk(Clk), .D(multiplexer_8_out), .Q(Address[4]));  // open: Qn, preset, en, reset
  D_Flip_Flop d_ff_9 (.clk(Clk), .D(multiplexer_9_out), .Q(Address[3]));  // open: Qn, preset, en, reset
  D_Flip_Flop d_ff_10 (.clk(Clk), .D(multiplexer_10_out), .Q(Address[2]));  // open: Qn, preset, en, reset
  D_Flip_Flop d_ff_11 (.clk(Clk), .D(multiplexer_11_out), .Q(Address[1]));  // open: Qn, preset, en, reset
  D_Flip_Flop d_ff_12 (.clk(Clk), .D(multiplexer_12_out), .Q(Address[0]));  // open: Qn, preset, en, reset

  assign Bus_In[14:12] = {3{Bus_In[15]}};
  assign Bus_Out = {4'b0000, Address};
  // also tied to GND on the sheet: Bus_In[15]
endmodule

module FlipFlop (
  input  Clk,
  input  D,
  input  Clr,
  input  set,
  output Q
);

  D_Flip_Flop d_ff_1 (.clk(Clk), .D(D), .Q(Q), .preset(set), .reset(Clr));  // open: Qn, en
endmodule

module Control_AR (
  input  R,
  input  T0,
  input  T2,
  input  T3,
  input  I,
  input  D7,
  input  D5,
  input  T4,
  output LD,
  output CLR,
  output INR
);

  wire and_3_out, not_1_out, not_2_out, or_1_out, or_2_out;

  not not_1 (not_1_out, R);
  or or_1 (or_1_out, T0, T2);
  and and_1 (CLR, R, T0);
  and and_2 (INR, D5, T4);
  and and_3 (and_3_out, not_1_out, or_1_out);
  not not_2 (not_2_out, D7);
  or or_2 (or_2_out, T3, I, not_2_out);
  or or_3 (LD, and_3_out, or_2_out);
endmodule
